// Logisim project guess-the-number-x.circ as structural Verilog
module decoder (
  input  A,
  input  B,
  input  C,
  input  D,
  output up1,
  output up2,
  output up3,
  output up4,
  output down1,
  output down2,
  output down3,
  output down4
);

  wire and_1_out, and_2_out, and_3_out, and_4_out, and_5_out, and_6_out, and_7_out, and_8_out, and_9_out,
       and_10_out, and_11_out, and_12_out, and_13_out, and_14_out, and_15_out, and_16_out, and_17_out,
       and_18_out, and_19_out, and_20_out, and_21_out, and_22_out, and_23_out, and_24_out, and_25_out,
       and_26_out, and_27_out, and_28_out, and_29_out, and_30_out, and_31_out, and_32_out, and_33_out,
       and_34_out, and_35_out, not_1_out, not_2_out, not_3_out, not_4_out;

  not not_1 (not_1_out, A);
  not not_2 (not_2_out, B);
  not not_3 (not_3_out, C);
  not not_4 (not_4_out, D);
  and and_1 (and_1_out, not_2_out, not_4_out);
  and and_2 (and_2_out, not_1_out, C);
  and and_3 (and_3_out, not_1_out, B, D);
  and and_4 (and_4_out, A, not_2_out, not_3_out);
  and and_5 (and_5_out, A, not_4_out);
  and and_6 (and_6_out, B, C);
  and and_7 (and_7_out, not_1_out, not_3_out, not_4_out);
  and and_8 (and_8_out, not_1_out, C, D);
  and and_9 (and_9_out, not_2_out, not_4_out);
  and and_10 (and_10_out, A, not_3_out, D);
  and and_11 (and_11_out, not_1_out, not_2_out);
  and and_12 (and_12_out, not_1_out, B);
  and and_13 (and_13_out, A, not_2_out);
  and and_14 (and_14_out, not_3_out, D);
  and and_15 (and_15_out, not_2_out, not_3_out);
  and and_16 (and_16_out, not_2_out, D);
  and and_17 (and_17_out, B, not_3_out, D);
  and and_18 (and_18_out, not_1_out, not_2_out, not_4_out);
  and and_19 (and_19_out, not_2_out, C, D);
  and and_20 (and_20_out, A, not_3_out);
  and and_21 (and_21_out, B, C, not_4_out);
  and and_22 (and_22_out, not_2_out, not_4_out);
  and and_23 (and_23_out, C, not_4_out);
  and and_24 (and_24_out, A, C);
  and and_25 (and_25_out, A, B);
  and and_26 (and_26_out, not_3_out, not_4_out);
  and and_27 (and_27_out, not_1_out, B, not_3_out);
  and and_28 (and_28_out, B, not_4_out);
  and and_29 (and_29_out, A, not_2_out);
  and and_30 (and_30_out, A, C);
  and and_31 (and_31_out, not_2_out, C);
  and and_32 (and_32_out, A, not_2_out);
  and and_33 (and_33_out, not_1_out, B, not_3_out);
  and and_34 (and_34_out, C, not_4_out);
  and and_35 (and_35_out, A, D);
  or or_1 (up3, and_1_out, and_2_out, and_3_out, and_4_out, and_5_out, and_6_out);
  or or_2 (up4, and_7_out, and_8_out, and_9_out, and_10_out, and_11_out);
  or or_3 (down3, and_12_out, and_13_out, and_14_out, and_15_out, and_16_out);
  or or_4 (down2, and_17_out, and_18_out, and_19_out, and_20_out, and_21_out);
  or or_5 (down1, and_22_out, and_23_out, and_24_out, and_25_out);
  or or_6 (up2, and_26_out, and_27_out, and_28_out, and_29_out, and_30_out);
  or or_7 (up1, and_31_out, and_32_out, and_33_out, and_34_out, and_35_out);

  assign down4 = 1'b0;

  // Notes on the sheet:
  //   UP 1
  //   UP 2
  //   UP 3
  //   UP 4
  //   DOWN 1
  //   DOWN 2
  //   DOWN 3
  //   DOWN 4
endmodule

module cronometro (
  input  clk,
  input  c_jogando,
  input  cfg,
  input  s0,
  input  s1,
  input  m0,
  input  m1,
  input  reset,
  output Fim_C,
  output [3:0] S0c,
  output [3:0] S1c,
  output [3:0] M0c,
  output [3:0] M1c
);

  wire and_1_out, borrows0, borrows1, borrows2, comparator_1_eq, comparator_2_eq, comparator_3_eq,
       comparator_4_eq, multiplexer_1_out, multiplexer_2_out, multiplexer_3_out, multiplexer_4_out,
       not_1_out, not_2_out;

  not not_1 (not_1_out, Fim_C);
  not not_2 (not_2_out, cfg);
  and and_1 (and_1_out, not_1_out, clk, c_jogando, not_2_out);
  Multiplexer #(.enable("false")) multiplexer_1 (.in0(and_1_out), .in1(s0), .out(multiplexer_1_out), .sel(cfg));
  Multiplexer #(.enable("false")) multiplexer_2 (.in0(borrows0), .in1(s1), .out(multiplexer_2_out), .sel(cfg));
  Multiplexer #(.enable("false")) multiplexer_3 (.in0(borrows1), .in1(m0), .out(multiplexer_3_out), .sel(cfg));
  Multiplexer #(.enable("false")) multiplexer_4 (.in0(borrows2), .in1(m1), .out(multiplexer_4_out), .sel(cfg));
  Comparator #(.width(4)) comparator_1 (.a(4'b0000), .b(S0c), .eq(comparator_1_eq));  // open: gt, lt
  Comparator #(.width(4)) comparator_2 (.a(4'b0000), .b(S1c), .eq(comparator_2_eq));  // open: gt, lt
  Comparator #(.width(4)) comparator_3 (.a(4'b0000), .b(M0c), .eq(comparator_3_eq));  // open: gt, lt
  Comparator #(.width(4)) comparator_4 (.a(4'b0000), .b(M1c), .eq(comparator_4_eq));  // open: gt, lt
  Counter #(.width(4), .max('h9)) u_s0 (
    .Q(S0c), .carry(borrows0), .clk(multiplexer_1_out), .clr(reset), .down(1'b1));  // open: load, D, count, preset
  Counter #(.width(4), .max('h5), .trigger("falling")) u_s1 (
    .Q(S1c), .carry(borrows1), .clk(multiplexer_2_out), .clr(reset), .down(1'b1));  // open: load, D, count, preset
  Counter #(.width(4), .max('h9), .trigger("falling")) u_m0 (
    .Q(M0c), .carry(borrows2), .clk(multiplexer_3_out), .clr(reset), .down(1'b1));  // open: load, D, count, preset
  Counter #(.width(4), .max('h5), .trigger("falling")) u_m1 (
    .Q(M1c), .clk(multiplexer_4_out), .clr(reset), .down(1'b1));  // open: load, D, count, carry, preset
  and and_2 (Fim_C, comparator_1_eq, comparator_2_eq, comparator_3_eq, comparator_4_eq);

  // Other names for the same wires on the sheet: fim = Fim_C; modo = cfg; saidam0[3:0] = M0c; saidam1[3:0] = M1c;
  //   saidas0[3:0] = S0c; saidas1[3:0] = S1c

  // Notes on the sheet:
  //   clock
  //   0 jogo$1 config
  //   MUDAR NO MODO $CONFIG
  //   CONDICOES JOGO
  //   +CLOCK
  //   FIM
  //   SAIDAS
endmodule

module gnx (
  input  Confirmar,
  input  Novo_N,
  input  [3:0] X,
  input  [3:0] Y,
  output X_certo,
  output Y_certo,
  output Soma_certa,
  output [7:0] Vermelho,
  output [7:0] Azul
);

  wire and_4_out, and_5_out, comparator_1_eq, comparator_2_eq, comparator_3_eq, comparator_4_eq,
       comparator_4_gt, comparator_5_lt, not_1_out, or_1_out;
  wire [3:0] adder_1_out, adder_2_out;
  wire [4:0] multiplexer_1_out, subtractor_1_out, subtractor_2_out;
  wire [4:4] adder_1_cout, adder_2_cout;
  wire [7:0] random_1_out;

  Random random_1 (.clk(Novo_N), .out(random_1_out));  // open: next, clr
  Adder #(.width(4)) adder_1 (.a(Y), .b(X), .out(adder_1_out), .cout(adder_1_cout[4]));  // open: cin
  Adder #(.width(4)) adder_2 (
    .a(random_1_out[7:4]), .b(random_1_out[3:0]), .out(adder_2_out), .cout(adder_2_cout[4]));  // open: cin
  Comparator #(.width(4)) comparator_1 (.a(random_1_out[3:0]), .b(X), .eq(comparator_1_eq));  // open: gt, lt
  and and_1 (X_certo, comparator_1_eq, Confirmar);
  Comparator #(.width(4)) comparator_2 (.a(random_1_out[7:4]), .b(Y), .eq(comparator_2_eq));  // open: gt, lt
  and and_2 (Y_certo, comparator_2_eq, Confirmar);
  Comparator #(.width(5)) comparator_3 (
    .a({adder_2_cout[4], adder_2_out}), .b({adder_1_cout[4], adder_1_out}), .eq(comparator_3_eq));  // open: gt, lt
  and and_3 (Soma_certa, Confirmar, comparator_3_eq);
  Comparator #(.width(5)) comparator_4 (
    .a({adder_2_cout[4], adder_2_out}), .b({adder_1_cout[4], adder_1_out}), .gt(comparator_4_gt),
    .eq(comparator_4_eq));  // open: lt
  Subtractor #(.width(5)) subtractor_1 (
    .a({adder_2_cout[4], adder_2_out}), .b({adder_1_cout[4], adder_1_out}), .out(subtractor_1_out));  // open: bin, bout
  Subtractor #(.width(5)) subtractor_2 (
    .a({adder_1_cout[4], adder_1_out}), .b({adder_2_cout[4], adder_2_out}), .out(subtractor_2_out));  // open: bin, bout
  and and_4 (and_4_out, Confirmar, or_1_out);
  and and_5 (and_5_out, Confirmar, not_1_out);
  not not_1 (not_1_out, or_1_out);
  assign Vermelho = {{7{and_4_out}}, and_4_out};  // Bit_Extender bit_extender_1
  assign Azul = {{7{and_5_out}}, and_5_out};  // Bit_Extender bit_extender_2
  Multiplexer #(.width(5), .enable("false")) multiplexer_1 (
    .in0(subtractor_1_out), .in1(subtractor_2_out), .out(multiplexer_1_out), .sel(comparator_4_gt));
  Comparator #(.width(5)) comparator_5 (.a(multiplexer_1_out), .b(5'b00101), .lt(comparator_5_lt));  // open: gt, eq
  or or_1 (or_1_out, comparator_4_eq, comparator_5_lt);

  // Notes on the sheet:
  //   r
  //   b
endmodule

module core (
  input  \Avançar ,
  input  Jogando,
  input  Fim_A,
  input  Fim_B,
  input  C_A,
  input  [3:0] V_A,
  input  Reset,
  input  Acerto,
  input  [3:0] V_B,
  input  C_B,
  output A_Jogando,
  output Jogando_X,
  output B_Jogando,
  output Jogando_Y,
  output [7:0] r,
  output [7:0] b,
  output Soma_Certa,
  output X_Certo,
  output Y_Certo,
  output [3:0] X_atual,
  output [3:0] Y_atual
);

  wire ACONFIRMADO, and_1_out, and_2_out, and_3_out, and_4_out, and_5_out, and_9_out, and_10_out, and_14_out,
       and_15_out, BCONFIRMADO, nor_1_out, not_1_out, not_2_out, not_3_out, or_1_out, or_2_out, or_3_out,
       or_4_out, or_5_out, or_6_out, or_7_out, or_8_out, RESET_t;
  wire [1:0] counter_1_q;
  wire [3:0] MUX;

  and and_1 (and_1_out, \Avançar , Jogando);
  or or_1 (or_1_out, counter_1_q[1], Fim_A);
  Counter #(.width(2), .max('h3)) counter_1 (
    .Q(counter_1_q), .clk(and_1_out), .clr(RESET_t));  // open: load, D, count, carry, preset, down
  and and_2 (and_2_out, or_1_out, not_1_out);
  not not_1 (not_1_out, Fim_B);
  not not_2 (not_2_out, and_2_out);
  not not_3 (not_3_out, counter_1_q[0]);
  nor nor_1 (nor_1_out, counter_1_q[0], and_2_out);
  and and_3 (and_3_out, not_2_out, counter_1_q[0]);
  and and_4 (and_4_out, and_2_out, not_3_out);
  and and_5 (and_5_out, and_2_out, counter_1_q[0]);
  Multiplexer #(.width(4), .enable("false")) multiplexer_1 (.in0(V_A), .in1(V_B), .out(MUX), .sel(B_Jogando));
  or or_2 (or_2_out, nor_1_out, and_3_out);
  and and_6 (A_Jogando, or_2_out, Jogando);
  or or_3 (or_3_out, and_4_out, and_5_out);
  and and_7 (B_Jogando, or_3_out, Jogando);
  or or_4 (or_4_out, nor_1_out, and_4_out);
  or or_5 (or_5_out, and_3_out, and_5_out);
  and and_8 (ACONFIRMADO, C_A, A_Jogando);
  and and_9 (and_9_out, C_B, B_Jogando);
  and and_10 (and_10_out, C_A, A_Jogando);
  and and_11 (BCONFIRMADO, C_B, B_Jogando);
  and and_12 (Jogando_X, or_4_out, Jogando);
  and and_13 (Jogando_Y, or_5_out, Jogando);
  or or_6 (or_6_out, ACONFIRMADO, and_9_out);
  or or_7 (or_7_out, and_10_out, BCONFIRMADO);
  or or_8 (or_8_out, ACONFIRMADO, BCONFIRMADO);
  and and_14 (and_14_out, or_6_out, Jogando_X);
  or or_9 (RESET_t, Reset, Acerto);
  and and_15 (and_15_out, Jogando_Y, or_7_out);
  gnx gnx_1 (
    .Confirmar(or_8_out), .X(X_atual), .Y(Y_atual), .Vermelho(r), .Azul(b), .X_certo(X_Certo),
    .Y_certo(Y_Certo), .Soma_certa(Soma_Certa));  // open: Novo_N
  Register #(.width(4), .Select("low")) X (.D(MUX), .en(and_14_out), .Q(X_atual), .clr(RESET_t));  // open: clk
  Register #(.width(4), .Select("low")) Y (.D(MUX), .en(and_15_out), .Q(Y_atual), .clk(RESET_t), .clr(RESET_t));

  // Other names for the same wires on the sheet: AJOGANDO = A_Jogando; BJOGANDO = B_Jogando; CONFIRMAA = C_A;
  //   CONFIRMAB = C_B; JOGANDOX = Jogando_X; JOGANDOY = Jogando_Y; XATUAL[3:0] = X_atual; YATUAL[3:0] = Y_atual

  // Notes on the sheet:
  //   LOGICA PARA FIM A
  //   PALPITE
  //   A JOGANDO X
  //   A JOGANDO Y
  //   B JOGANDO X
  //   B JOGANDO Y
  //   JOGANDO X
  //   JOGANDO Y
  //   CONDICAO X
  //   CONDICAO Y
  //   Red
  //   Blue
endmodule
